# Fritzing sketch Control_Digital (saved by Fritzing 0.9.3b)
breadboards: 1

parts:
  J1 = DHT22 temperature-humidity sensor [form="♂ (male)" package=THT]  # not connected
  M3 = BTS7960  # not connected
  BAT2 = 12 battery [package=battery]
  M4 = ESP32-S3-DevKitC-1-N8R8-v1 [part_number=ESP32-S3-DevKitC-1-N8R8-v1]
  A2 = WMYCONGCONG buck converter
  L298N1 = L298N DC motor driver  # not connected
  KY-1 = Keyes Relay [package=THT]  # not connected
  Halogen_Lapm1 = Halogen Lamp G4 [package="4 mm [THT]"]  # not connected
  M5 = seeed grove atomizer v1.0  # not connected

nets:
  N1: BAT2.-, A2.Pin_3
  N2: BAT2.+, A2.Pin_2
  N3: M4.pin_1, M4.pin_2
  N4: M4.pin_22, M4.pin_23, M4.pin_24, M4.pin_44

custom parts:
  DHT22 temperature-humidity sensor: The DHT22 is a basic, low-cost digital temperature and humidity sensor. It uses a capacitive humidity sensor and a thermistor to measure the surrounding air, and spits out a digital signal on the data pin (no analog input pins needed). It's fairly simple to use, but requires careful timing to grab data. The only real downside of this sensor is you can only get new data from it once every 2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
  BTS7960: BTS7960 43A Peak Power H-Bridge PWM Motor Driver
  12 battery: 12V lead acid type battery, like the Husqvarna YTH2448 12V 35AH battery. This is the mini version 1/4 the size of the actual battery to be closer to typical breadboard parts (around 2in wide rathher than 7in). The pads in pcb are sized to accomidate up to 14ga wire (as these batterys will deliver high currents.)
  ESP32-S3-DevKitC-1-N8R8-v1: ESP32-S3-DevKitC-1-N8R8-v1 This module is 44pins long (2x22) and 11 pins width.
  WMYCONGCONG buck converter: These amazing little DC-DC converters feature a wide input voltage of 4.5-24V and the output voltage can be set to one of six fixed voltages, or fully variable, just by bridging the relevant solder pads on the back of the PCB..
  L298N DC motor driver: 2x DC motor driver with 78M05 positive voltage regulator (7..35 V) L298N: max 46 V, 2 A Set 5 V Enable jumper to enable 5 V regultor (needed for the L298N) and +5 V output at screw terminal or supply external +5 V at screw terminal Set ENA and/or ENB to +5 V to enable motor permanently or supply ENA and/or ENB with PWM signal IN1 and IN2 set rotation directory for motor A (OUT1/OUT2) IN2 and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
  Keyes Relay: The Keyes 5V relay module is suitable for SCM development, home appliance control. It uses a 5V~12V TIL control signal which can control DC / AC signal.
  Halogen Lamp G4: A generic Halogen Lamp with G4 socket. Typical operating voltage around 12v and power around 20W
  seeed grove atomizer v1.0: Grove - Water Atomization is a perfect module for you to quickly DIY a humidifier with Arduino. You can also develop more advanced and interesting projects with digital scent technology and any other situations in which atomization required.
